// Logisim project 16 ALU.circ as structural Verilog: 5 circuits, main circuit main
module main (
  input  Cin,
  input  [15:0] A,
  input  [15:0] B,
  input  [1:0] S1_S0,
  input  IL,
  input  IR,
  output Cout
);

  wire [15:0] n16_bit_alu_1_output;

  _16_bit_alu u_16_bit_alu_1 (
    .A(A), .Cin(IL), .B(B), .S1_S0(S1_S0), .Output(n16_bit_alu_1_output), .IL(Cin), .IR(IR), .Cout(Cout));
  RAM #(.addrWidth(16), .dataWidth(16)) ram_1 (.addr(n16_bit_alu_1_output));  // open: data, sel, clk, ld, clr
endmodule

// Arith
module arith (
  input  in_1,
  input  [15:0] a,
  input  [15:0] b,
  input  [1:0] in_4,
  output [15:0] out_5,
  output out_6
);

  wire [15:0] multiplexer_1_out, not_1_out;

  assign not_1_out = ~b;  // NOT_Gate not_1, 16 bits wide
  Multiplexer #(.select(2), .width(16), .enable("false")) multiplexer_1 (
    .in0(b), .in1(not_1_out), .in2({16{1'b0}}), .in3({16{1'b1}}), .out(multiplexer_1_out), .sel(in_4));
  Adder #(.width(16)) adder_1 (.a(a), .b(multiplexer_1_out), .out(out_5), .cin(in_1), .cout(out_6));
endmodule

// Logic
module \logic  (
  input  [15:0] a,
  input  [15:0] b,
  input  [1:0] s1_s0,
  output [15:0] out_4
);

  wire [15:0] and_1_out, not_1_out, or_1_out, xor_1_out;

  assign and_1_out = a & b;  // AND_Gate and_1, 16 bits wide
  assign xor_1_out = a ^ b;  // XOR_Gate xor_1, 16 bits wide
  assign or_1_out = a | b;  // OR_Gate or_1, 16 bits wide
  assign not_1_out = ~a;  // NOT_Gate not_1, 16 bits wide
  Multiplexer #(.select(2), .width(16), .enable("false")) multiplexer_1 (
    .in0(and_1_out), .in1(or_1_out), .in2(xor_1_out), .in3(not_1_out), .out(out_4), .sel(s1_s0));
endmodule

// Shift
module shift (
  input  IL,
  input  [15:0] INPUT,
  input  IR,
  output [15:0] LS,
  output [15:0] RS
);


  assign LS = {INPUT[14:0], IL};
  assign RS = {IR, INPUT[15:1]};
endmodule

// 16 bit ALU
module _16_bit_alu (
  input  [15:0] A,
  input  Cin,
  input  [15:0] B,
  input  IL,
  input  [1:0] S1_S0,
  input  IR,
  output [15:0] Output,
  output Cout
);

  wire [15:0] arith_1_out_5, logic_1_out_4, shift_1_ls, shift_1_rs;

  shift shift_1 (.INPUT(A), .IL(IL), .IR(IR), .LS(shift_1_ls), .RS(shift_1_rs));
  arith arith_1 (.in_1(Cin), .a(A), .b(B), .in_4(S1_S0), .out_6(Cout), .out_5(arith_1_out_5));
  \logic  logic_1 (.a(A), .b(B), .s1_s0(S1_S0), .out_4(logic_1_out_4));
  Multiplexer #(.select(2), .width(16)) multiplexer_1 (
    .in0(arith_1_out_5), .in1(logic_1_out_4), .in2(shift_1_ls), .in3(shift_1_rs), .out(Output), .sel(S1_S0));  // open: en
endmodule
